// Logisim project SR_Latch_NAND.circ as structural Verilog: 1 circuit, main circuit main
module main (
  input  S,
  input  R,
  output out_3,
  output out_4
);

  nand nand_1 (out_3, S, out_4);
  nand nand_2 (out_4, out_3, R);
endmodule
