// Logisim project SR_Latch_NOR.circ as structural Verilog: 1 circuit, main circuit main
module main (
  input  R,
  input  S,
  output out_3,
  output out_4
);

  nor nor_1 (out_3, R, out_4);
  nor nor_2 (out_4, out_3, S);
endmodule
